# Fritzing sketch piezoTone (saved by Fritzing 0.8.0b)
breadboards: 1

parts:
  Part1 = Arduino Uno (Rev3)
  R1 = Resistor [tolerance=±5% resistance=220 package=THT]
  LED1 = LED - 5mm [color="Red (633nm)" package="5 mm [THT]"]
  piezo_element = Piezo Speaker

nets:
  N1: Part1.GND, R1.Pin_1, piezo_element.pin1
  N2: Part1.D9_PWM, LED1.anode
  N3: Part1.D10_PWM/SS, piezo_element.pin2
  N4: R1.Pin_0, LED1.cathode

notes:
  If headphones are used in place of the piezo element then a 220 or 330 ohm resistor should be added between the headphone plug and ground
