# Fritzing sketch 8ohmSpeaker (saved by Fritzing 0.8.0b)
breadboards: 1

parts:
  SPKR1 = Loudspeaker
  R1 = Resistor [tolerance=±5% resistance=220 package=THT]
  Part1 = Arduino Uno (Rev3)

nets:
  N1: SPKR1.pin1, Part1.GND
  N2: SPKR1.pin2, R1.Pin_0
  N3: R1.Pin_1, Part1.D10_PWM/SS
