# Fritzing sketch 8ohmSpeaker (saved by Fritzing 0.8.0b)

parts:
  SPKR1 = Loudspeaker
  Part1 = Arduino Uno (Rev3)
  R1 = Resistor [tolerance=±5% resistance=220 package=THT]
  LED1 = LED - 5mm [color="Red (633nm)" package="5 mm [THT]"]
  R2 = Resistor [tolerance=±5% resistance=220 package=THT]

nets:
  N1: SPKR1.pin1, Part1.GND, R2.Pin_1
  N2: SPKR1.pin2, R1.Pin_0
  N3: Part1.D9_PWM, LED1.anode
  N4: Part1.D10_PWM/SS, R1.Pin_1
  N5: LED1.cathode, R2.Pin_0
